# Fritzing sketch breadboard (saved by Fritzing 0.8.3b)
circuit board: 16.9333cm x 5.64444cm
breadboards: 1

parts:
  Part1 = Arduino Uno (Rev3)
  XTAL1 = CRYSTAL - kHz [frequency="32 kHz"]
  IC2 = DS1302 [package="DIP8 [THT]"]

nets:
  N1: Part1.GND, IC2.0V
  N2: Part1.D5_PWM, IC2.CE_-_Chip_Enable
  N3: Part1.D6_PWM, IC2.I/O_-_SPI_Data_In/Out
  N4: Part1.D7, IC2.SCLK_-_SPI_Clock
  N5: Part1.5V, IC2.+V
  N6: XTAL1.pin_0, IC2.X2_-_Crystal
  N7: XTAL1.pin_1, IC2.X1_-_Crystal
